// Logisim project calculadora - Copia.circ as structural Verilog: 5 circuits, main circuit conversor
module conversor (
  input  a,
  input  b,
  input  c,
  input  d,
  input  e,
  input  f,
  input  g,
  output X4,
  output X3,
  output X2,
  output X1
);

  wire and_1_out, and_2_out, and_3_out, and_4_out, and_5_out, and_6_out, and_7_out, and_8_out, and_9_out,
       and_10_out, and_11_out, and_12_out, and_13_out, and_14_out, and_15_out, and_16_out, and_17_out,
       and_18_out, and_19_out, and_20_out, and_21_out, and_22_out, and_23_out, not_1_out, not_2_out,
       not_3_out, not_4_out, not_5_out, not_6_out, not_7_out, not_8_out, not_9_out, not_10_out, not_11_out,
       not_12_out, not_13_out, not_14_out, not_15_out, not_16_out, not_17_out, not_18_out, not_19_out,
       not_20_out, not_21_out, not_22_out, not_23_out, not_24_out, not_25_out, not_26_out, not_27_out,
       not_28_out, not_29_out, not_30_out, not_31_out, not_32_out, not_33_out, not_34_out, not_35_out,
       not_36_out, not_37_out, not_38_out, not_39_out, not_40_out, not_41_out, not_42_out, not_43_out,
       not_44_out, not_45_out, not_46_out;

  not not_1 (not_1_out, a);
  not not_2 (not_2_out, b);
  not not_3 (not_3_out, f);
  not not_4 (not_4_out, b);
  not not_5 (not_5_out, c);
  not not_6 (not_6_out, b);
  not not_7 (not_7_out, c);
  not not_8 (not_8_out, a);
  not not_9 (not_9_out, d);
  not not_10 (not_10_out, e);
  not not_11 (not_11_out, a);
  not not_12 (not_12_out, f);
  not not_13 (not_13_out, b);
  not not_14 (not_14_out, c);
  not not_15 (not_15_out, b);
  not not_16 (not_16_out, c);
  not not_17 (not_17_out, b);
  not not_18 (not_18_out, d);
  not not_19 (not_19_out, e);
  not not_20 (not_20_out, f);
  not not_21 (not_21_out, g);
  not not_22 (not_22_out, b);
  not not_23 (not_23_out, b);
  not not_24 (not_24_out, c);
  not not_25 (not_25_out, c);
  not not_26 (not_26_out, f);
  not not_27 (not_27_out, d);
  not not_28 (not_28_out, e);
  not not_29 (not_29_out, f);
  not not_30 (not_30_out, g);
  not not_31 (not_31_out, d);
  not not_32 (not_32_out, e);
  not not_33 (not_33_out, f);
  not not_34 (not_34_out, a);
  not not_35 (not_35_out, b);
  not not_36 (not_36_out, d);
  not not_37 (not_37_out, e);
  not not_38 (not_38_out, f);
  not not_39 (not_39_out, g);
  not not_40 (not_40_out, f);
  not not_41 (not_41_out, b);
  not not_42 (not_42_out, c);
  not not_43 (not_43_out, d);
  not not_44 (not_44_out, b);
  not not_45 (not_45_out, e);
  not not_46 (not_46_out, f);
  and and_1 (and_1_out, not_1_out, not_2_out, c, d, e, f, g);
  and and_2 (and_2_out, b, c, d, e, not_3_out, g);
  and and_3 (and_3_out, a, not_4_out, not_5_out, e, f, g);
  and and_4 (and_4_out, a, not_6_out, not_7_out, d, e, f);
  and and_5 (and_5_out, a, b, c, e, f, g);
  and and_6 (and_6_out, not_8_out, b, c, not_9_out, not_10_out, f, g);
  and and_7 (and_7_out, not_11_out, b, c, d, e, not_12_out, g);
  and and_8 (and_8_out, a, not_13_out, not_14_out, e, f, g);
  and and_9 (and_9_out, a, not_15_out, not_16_out, d, e, f);
  and and_10 (and_10_out, a, not_17_out, c, d, f, g);
  and and_11 (and_11_out, a, b, c, not_18_out, not_19_out, not_20_out, not_21_out);
  and and_12 (and_12_out, not_22_out, c, d, e, f, g);
  and and_13 (and_13_out, a, not_23_out, not_24_out, e, f, g);
  and and_14 (and_14_out, a, b, not_25_out, d, e, not_26_out, g);
  and and_15 (and_15_out, a, b, c, not_27_out, not_28_out, not_29_out, not_30_out);
  and and_16 (and_16_out, a, b, c, not_31_out, e, f, g);
  and and_17 (and_17_out, a, b, c, d, not_32_out, not_33_out, g);
  and and_18 (and_18_out, not_34_out, not_35_out, c, d, e, f, g);
  and and_19 (and_19_out, b, c, not_36_out, not_37_out, not_38_out, not_39_out);
  and and_20 (and_20_out, b, c, d, e, not_40_out, g);
  and and_21 (and_21_out, a, not_41_out, not_42_out, not_43_out, e, f, g);
  and and_22 (and_22_out, a, not_44_out, c, d, not_45_out, f, g);
  and and_23 (and_23_out, a, b, c, d, not_46_out, g);
  or or_1 (X4, and_1_out, and_2_out, and_3_out, and_4_out, and_5_out);
  or or_2 (X3, and_6_out, and_7_out, and_8_out, and_9_out, and_10_out, and_11_out);
  or or_3 (X2, and_12_out, and_13_out, and_14_out, and_15_out, and_16_out, and_17_out);
  or or_4 (X1, and_18_out, and_19_out, and_20_out, and_21_out, and_22_out, and_23_out);
endmodule

module main (
  input  in_1,
  input  in_2,
  input  in_3,
  input  in_4,
  input  in_5,
  input  in_6,
  input  in_7,
  input  in_8,
  input  in_9,
  input  in_10,
  input  in_11,
  input  in_12,
  input  in_13,
  input  in_14,
  input  in_15,
  input  in_16,
  output X4,
  output X3,
  output X2,
  output X1,
  output Y4,
  output Y3,
  output Y2,
  output Y1
);

  _7_Segment_Display u_7_segment_display_1 (
    .g(in_4), .f(in_2), .a(in_1), .b(in_3), .e(in_5), .d(in_7), .c(in_6));  // open: dp
  _7_Segment_Display u_7_segment_display_2 (
    .g(in_11), .f(in_9), .a(in_8), .b(in_10), .e(in_14), .d(in_16), .c(in_15));  // open: dp
  conversor conversor_1 (
    .a(in_1), .b(in_3), .c(in_6), .d(in_7), .e(in_5), .f(in_2), .g(in_4), .X4(X4), .X3(X3), .X2(X2), .X1(X1));
  conversor conversor_2 (
    .a(in_8), .b(in_10), .c(in_15), .d(in_16), .e(in_14), .f(in_9), .g(in_11), .X4(Y4), .X3(Y3), .X2(Y2),
    .X1(Y1));
  calculador calculador_1 ();
endmodule

module soma (
  input  X4,
  input  X3,
  input  X2,
  input  X1,
  input  Y4,
  input  Y3,
  input  Y2,
  input  Y1,
  output Z4,
  output Z3,
  output Z2,
  output Z1,
  output ERRO
);

  wire and_1_out, and_2_out, and_3_out, and_4_out, and_5_out, and_6_out, and_7_out, and_8_out, and_9_out,
       and_10_out, and_11_out, and_12_out, and_13_out, and_14_out, and_15_out, and_16_out, and_17_out,
       and_18_out, and_19_out, and_20_out, and_21_out, and_22_out, and_23_out, and_24_out, and_25_out,
       and_26_out, and_27_out, and_28_out, and_29_out, and_30_out, and_31_out, and_32_out, and_33_out,
       and_34_out, and_35_out, and_36_out, and_37_out, and_38_out, and_39_out, and_40_out, and_41_out,
       and_42_out, and_43_out, and_44_out, and_45_out, and_46_out, and_47_out, and_48_out, and_49_out,
       and_50_out, and_51_out, and_52_out, and_53_out, and_54_out, and_55_out, and_56_out, and_57_out,
       and_58_out, and_59_out, and_60_out, and_61_out, and_62_out, and_63_out, and_64_out, and_65_out,
       and_66_out, and_67_out, and_68_out, and_69_out, and_70_out, and_71_out, and_72_out, and_73_out,
       and_74_out, and_75_out, and_76_out, and_77_out, and_78_out, and_79_out, and_80_out, and_81_out,
       and_82_out, and_83_out, and_84_out, and_85_out, and_86_out, and_87_out, and_88_out, and_89_out,
       and_90_out, and_91_out, and_92_out, and_93_out, and_94_out, and_95_out, and_96_out, and_97_out,
       and_98_out, and_99_out, and_100_out, and_101_out, and_102_out, and_103_out, and_104_out, and_105_out,
       and_106_out, and_107_out, and_108_out, and_109_out, and_110_out, and_111_out, and_112_out,
       and_113_out, and_114_out, and_115_out, and_116_out, and_117_out, and_118_out, and_119_out,
       and_120_out, and_121_out, and_122_out, and_123_out, not_1_out, not_2_out, not_3_out, not_4_out,
       not_5_out, not_6_out, not_7_out, not_8_out, not_9_out, not_10_out, not_11_out, not_12_out, not_13_out,
       not_14_out, not_15_out, not_16_out, not_17_out, not_18_out, not_19_out, not_20_out, not_21_out,
       not_22_out, not_23_out, not_24_out, not_25_out, not_26_out, not_27_out, not_28_out, not_29_out,
       not_30_out, not_31_out, not_32_out, not_33_out, not_34_out, not_35_out, not_36_out, not_37_out,
       not_38_out, not_39_out, not_40_out, not_41_out, not_42_out, not_43_out, not_44_out, not_45_out,
       not_46_out, not_47_out, not_48_out, not_49_out, not_50_out, not_51_out, not_52_out, not_53_out,
       not_54_out, not_55_out, not_56_out, not_57_out, not_58_out, not_59_out, not_60_out, not_61_out,
       not_62_out, not_63_out, not_64_out, not_65_out, not_66_out, not_67_out, not_68_out, not_69_out,
       not_70_out, not_71_out, not_72_out, not_73_out, not_74_out, not_75_out, not_76_out, not_77_out,
       not_78_out, not_79_out, not_80_out, not_81_out, not_82_out, not_83_out, not_84_out, not_85_out,
       not_86_out, not_87_out, not_88_out, not_89_out, not_90_out, not_91_out, not_92_out, not_93_out,
       not_94_out, not_95_out, not_96_out, not_97_out, not_98_out, not_99_out, not_100_out, not_101_out,
       not_102_out, not_103_out, not_104_out, not_105_out, not_106_out, not_107_out, not_108_out,
       not_109_out, not_110_out, not_111_out, not_112_out, not_113_out, not_114_out, not_115_out,
       not_116_out, not_117_out, not_118_out, not_119_out, not_120_out, not_121_out, not_122_out,
       not_123_out, not_124_out, not_125_out, not_126_out, not_127_out, not_128_out, not_129_out,
       not_130_out, not_131_out, not_132_out, not_133_out, not_134_out, not_135_out, not_136_out,
       not_137_out, not_138_out, not_139_out, not_140_out, not_141_out, not_142_out, not_143_out,
       not_144_out, not_145_out, not_146_out, not_147_out, not_148_out, not_149_out, not_150_out,
       not_151_out, not_152_out, not_153_out, not_154_out, not_155_out, not_156_out, not_157_out,
       not_158_out, not_159_out, not_160_out, not_161_out, not_162_out, not_163_out, not_164_out,
       not_165_out, not_166_out, not_167_out, not_168_out, not_169_out, not_170_out, not_171_out,
       not_172_out, not_173_out, not_174_out, not_175_out, not_176_out, not_177_out, not_178_out,
       not_179_out, not_180_out, not_181_out, not_182_out, not_183_out, not_184_out, not_185_out,
       not_186_out, not_187_out, not_188_out, not_189_out, not_190_out, not_191_out, not_192_out,
       not_193_out, not_194_out, not_195_out, not_196_out, not_197_out, not_198_out, not_199_out,
       not_200_out, not_201_out, not_202_out, not_203_out, not_204_out, not_205_out, not_206_out,
       not_207_out, not_208_out, not_209_out, not_210_out, not_211_out, not_212_out, not_213_out,
       not_214_out, not_215_out, not_216_out, not_217_out, not_218_out, not_219_out, not_220_out,
       not_221_out, not_222_out, not_223_out, not_224_out, not_225_out, not_226_out, not_227_out,
       not_228_out, not_229_out, not_230_out, not_231_out, not_232_out, not_233_out, not_234_out,
       not_235_out, not_236_out, not_237_out, not_238_out, not_239_out, not_240_out, not_241_out,
       not_242_out, not_243_out, not_244_out, not_245_out, not_246_out, not_247_out, not_248_out,
       not_249_out, not_250_out, not_251_out, not_252_out, not_253_out, not_254_out, not_255_out,
       not_256_out, not_257_out, not_258_out, not_259_out, not_260_out, not_261_out, not_262_out,
       not_263_out, not_264_out, not_265_out, not_266_out, not_267_out, not_268_out, not_269_out,
       not_270_out, not_271_out, not_272_out, not_273_out, not_274_out, not_275_out, not_276_out,
       not_277_out, not_278_out, not_279_out, not_280_out, not_281_out, not_282_out, not_283_out,
       not_284_out, not_285_out, not_286_out, not_287_out, not_288_out, not_289_out, not_290_out,
       not_291_out, not_292_out, not_293_out, not_294_out, not_295_out, not_296_out, not_297_out,
       not_298_out, not_299_out, not_300_out, not_301_out, not_302_out, not_303_out, not_304_out,
       not_305_out, not_306_out, not_307_out, not_308_out, not_309_out, not_310_out, not_311_out,
       not_312_out, not_313_out, not_314_out, not_315_out, not_316_out, not_317_out, not_318_out,
       not_319_out, not_320_out, not_321_out, not_322_out, not_323_out, not_324_out, not_325_out,
       not_326_out, not_327_out, not_328_out, not_329_out, not_330_out, not_331_out, not_332_out,
       not_333_out, not_334_out, not_335_out, not_336_out, not_337_out, not_338_out, not_339_out,
       not_340_out, not_341_out, not_342_out, not_343_out, not_344_out, not_345_out, not_346_out,
       not_347_out, not_348_out, not_349_out, not_350_out, not_351_out, not_352_out, not_353_out,
       not_354_out, not_355_out, not_356_out, not_357_out, not_358_out, not_359_out, not_360_out,
       not_361_out, not_362_out, not_363_out, not_364_out, not_365_out, not_366_out, not_367_out,
       not_368_out, not_369_out, not_370_out, not_371_out, not_372_out, not_373_out, not_374_out,
       not_375_out, not_376_out, not_377_out, not_378_out, not_379_out, not_380_out, not_381_out,
       not_382_out, not_383_out, not_384_out, not_385_out, not_386_out, not_387_out, not_388_out,
       not_389_out, not_390_out, not_391_out, not_392_out, not_393_out, not_394_out, not_395_out,
       not_396_out, not_397_out, not_398_out;

  not not_1 (not_1_out, X4);
  not not_2 (not_2_out, X3);
  not not_3 (not_3_out, X2);
  not not_4 (not_4_out, X1);
  not not_5 (not_5_out, X4);
  not not_6 (not_6_out, X3);
  not not_7 (not_7_out, X2);
  not not_8 (not_8_out, Y2);
  not not_9 (not_9_out, X4);
  not not_10 (not_10_out, X3);
  not not_11 (not_11_out, X2);
  not not_12 (not_12_out, Y1);
  not not_13 (not_13_out, X4);
  not not_14 (not_14_out, X3);
  not not_15 (not_15_out, X1);
  not not_16 (not_16_out, Y2);
  not not_17 (not_17_out, X4);
  not not_18 (not_18_out, X3);
  not not_19 (not_19_out, Y3);
  not not_20 (not_20_out, X4);
  not not_21 (not_21_out, X3);
  not not_22 (not_22_out, Y2);
  not not_23 (not_23_out, Y1);
  not not_24 (not_24_out, X4);
  not not_25 (not_25_out, X2);
  not not_26 (not_26_out, X1);
  not not_27 (not_27_out, Y3);
  not not_28 (not_28_out, X4);
  not not_29 (not_29_out, X2);
  not not_30 (not_30_out, Y3);
  not not_31 (not_31_out, Y2);
  not not_32 (not_32_out, X4);
  not not_33 (not_33_out, X2);
  not not_34 (not_34_out, Y3);
  not not_35 (not_35_out, Y1);
  not not_36 (not_36_out, X4);
  not not_37 (not_37_out, X1);
  not not_38 (not_38_out, Y3);
  not not_39 (not_39_out, Y2);
  not not_40 (not_40_out, X4);
  not not_41 (not_41_out, Y3);
  not not_42 (not_42_out, Y2);
  not not_43 (not_43_out, Y1);
  not not_44 (not_44_out, X4);
  not not_45 (not_45_out, Y4);
  not not_46 (not_46_out, X4);
  not not_47 (not_47_out, Y4);
  not not_48 (not_48_out, X4);
  not not_49 (not_49_out, Y4);
  not not_50 (not_50_out, X4);
  not not_51 (not_51_out, Y4);
  not not_52 (not_52_out, X4);
  not not_53 (not_53_out, Y4);
  not not_54 (not_54_out, X4);
  not not_55 (not_55_out, Y4);
  not not_56 (not_56_out, X4);
  not not_57 (not_57_out, Y4);
  not not_58 (not_58_out, X3);
  not not_59 (not_59_out, X2);
  not not_60 (not_60_out, X1);
  not not_61 (not_61_out, Y4);
  not not_62 (not_62_out, X3);
  not not_63 (not_63_out, X2);
  not not_64 (not_64_out, Y4);
  not not_65 (not_65_out, Y2);
  not not_66 (not_66_out, X3);
  not not_67 (not_67_out, X2);
  not not_68 (not_68_out, Y4);
  not not_69 (not_69_out, Y1);
  not not_70 (not_70_out, X3);
  not not_71 (not_71_out, X1);
  not not_72 (not_72_out, Y4);
  not not_73 (not_73_out, Y2);
  not not_74 (not_74_out, X3);
  not not_75 (not_75_out, Y4);
  not not_76 (not_76_out, Y3);
  not not_77 (not_77_out, X3);
  not not_78 (not_78_out, Y4);
  not not_79 (not_79_out, Y2);
  not not_80 (not_80_out, Y1);
  not not_81 (not_81_out, X2);
  not not_82 (not_82_out, X1);
  not not_83 (not_83_out, Y4);
  not not_84 (not_84_out, Y3);
  not not_85 (not_85_out, X2);
  not not_86 (not_86_out, Y4);
  not not_87 (not_87_out, Y3);
  not not_88 (not_88_out, Y2);
  not not_89 (not_89_out, X2);
  not not_90 (not_90_out, Y4);
  not not_91 (not_91_out, Y3);
  not not_92 (not_92_out, Y1);
  not not_93 (not_93_out, X1);
  not not_94 (not_94_out, Y4);
  not not_95 (not_95_out, Y3);
  not not_96 (not_96_out, Y2);
  not not_97 (not_97_out, Y4);
  not not_98 (not_98_out, Y3);
  not not_99 (not_99_out, Y2);
  not not_100 (not_100_out, Y1);
  not not_101 (not_101_out, X4);
  not not_102 (not_102_out, X3);
  not not_103 (not_103_out, X2);
  not not_104 (not_104_out, X1);
  not not_105 (not_105_out, X4);
  not not_106 (not_106_out, X3);
  not not_107 (not_107_out, X2);
  not not_108 (not_108_out, Y2);
  not not_109 (not_109_out, X4);
  not not_110 (not_110_out, X3);
  not not_111 (not_111_out, X2);
  not not_112 (not_112_out, Y1);
  not not_113 (not_113_out, X4);
  not not_114 (not_114_out, X3);
  not not_115 (not_115_out, X1);
  not not_116 (not_116_out, Y2);
  not not_117 (not_117_out, X4);
  not not_118 (not_118_out, X3);
  not not_119 (not_119_out, Y2);
  not not_120 (not_120_out, Y1);
  not not_121 (not_121_out, X3);
  not not_122 (not_122_out, X2);
  not not_123 (not_123_out, X1);
  not not_124 (not_124_out, Y4);
  not not_125 (not_125_out, X3);
  not not_126 (not_126_out, X2);
  not not_127 (not_127_out, Y4);
  not not_128 (not_128_out, Y2);
  not not_129 (not_129_out, X3);
  not not_130 (not_130_out, X2);
  not not_131 (not_131_out, Y4);
  not not_132 (not_132_out, Y1);
  not not_133 (not_133_out, X3);
  not not_134 (not_134_out, X1);
  not not_135 (not_135_out, Y4);
  not not_136 (not_136_out, Y2);
  not not_137 (not_137_out, X3);
  not not_138 (not_138_out, Y4);
  not not_139 (not_139_out, Y2);
  not not_140 (not_140_out, Y1);
  not not_141 (not_141_out, X4);
  not not_142 (not_142_out, X3);
  not not_143 (not_143_out, Y3);
  not not_144 (not_144_out, X3);
  not not_145 (not_145_out, Y4);
  not not_146 (not_146_out, Y3);
  not not_147 (not_147_out, X4);
  not not_148 (not_148_out, X3);
  not not_149 (not_149_out, Y3);
  not not_150 (not_150_out, X3);
  not not_151 (not_151_out, Y4);
  not not_152 (not_152_out, Y3);
  not not_153 (not_153_out, X4);
  not not_154 (not_154_out, X3);
  not not_155 (not_155_out, Y3);
  not not_156 (not_156_out, X3);
  not not_157 (not_157_out, Y4);
  not not_158 (not_158_out, Y3);
  not not_159 (not_159_out, X4);
  not not_160 (not_160_out, X2);
  not not_161 (not_161_out, X1);
  not not_162 (not_162_out, Y3);
  not not_163 (not_163_out, X4);
  not not_164 (not_164_out, X2);
  not not_165 (not_165_out, Y3);
  not not_166 (not_166_out, Y2);
  not not_167 (not_167_out, X4);
  not not_168 (not_168_out, X2);
  not not_169 (not_169_out, Y3);
  not not_170 (not_170_out, Y1);
  not not_171 (not_171_out, X4);
  not not_172 (not_172_out, X1);
  not not_173 (not_173_out, Y3);
  not not_174 (not_174_out, Y2);
  not not_175 (not_175_out, X4);
  not not_176 (not_176_out, Y3);
  not not_177 (not_177_out, Y2);
  not not_178 (not_178_out, Y1);
  not not_179 (not_179_out, X2);
  not not_180 (not_180_out, X1);
  not not_181 (not_181_out, Y4);
  not not_182 (not_182_out, Y3);
  not not_183 (not_183_out, X2);
  not not_184 (not_184_out, Y4);
  not not_185 (not_185_out, Y3);
  not not_186 (not_186_out, Y2);
  not not_187 (not_187_out, X2);
  not not_188 (not_188_out, Y4);
  not not_189 (not_189_out, Y3);
  not not_190 (not_190_out, Y1);
  not not_191 (not_191_out, X1);
  not not_192 (not_192_out, Y4);
  not not_193 (not_193_out, Y3);
  not not_194 (not_194_out, Y2);
  not not_195 (not_195_out, Y4);
  not not_196 (not_196_out, Y3);
  not not_197 (not_197_out, Y2);
  not not_198 (not_198_out, Y1);
  not not_199 (not_199_out, X4);
  not not_200 (not_200_out, Y4);
  not not_201 (not_201_out, X4);
  not not_202 (not_202_out, Y4);
  not not_203 (not_203_out, X4);
  not not_204 (not_204_out, Y4);
  not not_205 (not_205_out, X4);
  not not_206 (not_206_out, X3);
  not not_207 (not_207_out, X2);
  not not_208 (not_208_out, X1);
  not not_209 (not_209_out, X4);
  not not_210 (not_210_out, X3);
  not not_211 (not_211_out, X2);
  not not_212 (not_212_out, Y1);
  not not_213 (not_213_out, X4);
  not not_214 (not_214_out, X2);
  not not_215 (not_215_out, X1);
  not not_216 (not_216_out, Y4);
  not not_217 (not_217_out, X4);
  not not_218 (not_218_out, X2);
  not not_219 (not_219_out, X1);
  not not_220 (not_220_out, Y3);
  not not_221 (not_221_out, X4);
  not not_222 (not_222_out, X2);
  not not_223 (not_223_out, Y4);
  not not_224 (not_224_out, Y1);
  not not_225 (not_225_out, X4);
  not not_226 (not_226_out, X2);
  not not_227 (not_227_out, Y3);
  not not_228 (not_228_out, Y1);
  not not_229 (not_229_out, X3);
  not not_230 (not_230_out, X2);
  not not_231 (not_231_out, X1);
  not not_232 (not_232_out, Y4);
  not not_233 (not_233_out, X3);
  not not_234 (not_234_out, X2);
  not not_235 (not_235_out, Y4);
  not not_236 (not_236_out, Y1);
  not not_237 (not_237_out, X2);
  not not_238 (not_238_out, X1);
  not not_239 (not_239_out, Y4);
  not not_240 (not_240_out, Y3);
  not not_241 (not_241_out, X2);
  not not_242 (not_242_out, Y4);
  not not_243 (not_243_out, Y3);
  not not_244 (not_244_out, Y1);
  not not_245 (not_245_out, X4);
  not not_246 (not_246_out, X3);
  not not_247 (not_247_out, X2);
  not not_248 (not_248_out, Y2);
  not not_249 (not_249_out, X4);
  not not_250 (not_250_out, X2);
  not not_251 (not_251_out, Y4);
  not not_252 (not_252_out, Y2);
  not not_253 (not_253_out, X4);
  not not_254 (not_254_out, X2);
  not not_255 (not_255_out, Y3);
  not not_256 (not_256_out, Y2);
  not not_257 (not_257_out, X3);
  not not_258 (not_258_out, X2);
  not not_259 (not_259_out, Y4);
  not not_260 (not_260_out, Y2);
  not not_261 (not_261_out, X2);
  not not_262 (not_262_out, Y4);
  not not_263 (not_263_out, Y3);
  not not_264 (not_264_out, Y2);
  not not_265 (not_265_out, X4);
  not not_266 (not_266_out, X3);
  not not_267 (not_267_out, X1);
  not not_268 (not_268_out, Y2);
  not not_269 (not_269_out, X4);
  not not_270 (not_270_out, X3);
  not not_271 (not_271_out, Y2);
  not not_272 (not_272_out, Y1);
  not not_273 (not_273_out, X4);
  not not_274 (not_274_out, X1);
  not not_275 (not_275_out, Y4);
  not not_276 (not_276_out, Y2);
  not not_277 (not_277_out, X4);
  not not_278 (not_278_out, X1);
  not not_279 (not_279_out, Y3);
  not not_280 (not_280_out, Y2);
  not not_281 (not_281_out, X4);
  not not_282 (not_282_out, Y4);
  not not_283 (not_283_out, Y2);
  not not_284 (not_284_out, Y1);
  not not_285 (not_285_out, X4);
  not not_286 (not_286_out, Y3);
  not not_287 (not_287_out, Y2);
  not not_288 (not_288_out, Y1);
  not not_289 (not_289_out, X3);
  not not_290 (not_290_out, X1);
  not not_291 (not_291_out, Y4);
  not not_292 (not_292_out, Y2);
  not not_293 (not_293_out, X3);
  not not_294 (not_294_out, Y4);
  not not_295 (not_295_out, Y2);
  not not_296 (not_296_out, Y1);
  not not_297 (not_297_out, X1);
  not not_298 (not_298_out, Y4);
  not not_299 (not_299_out, Y3);
  not not_300 (not_300_out, Y2);
  not not_301 (not_301_out, Y4);
  not not_302 (not_302_out, Y3);
  not not_303 (not_303_out, Y2);
  not not_304 (not_304_out, Y1);
  not not_305 (not_305_out, X4);
  not not_306 (not_306_out, X3);
  not not_307 (not_307_out, Y3);
  not not_308 (not_308_out, X4);
  not not_309 (not_309_out, Y4);
  not not_310 (not_310_out, X3);
  not not_311 (not_311_out, Y4);
  not not_312 (not_312_out, Y3);
  not not_313 (not_313_out, X4);
  not not_314 (not_314_out, X3);
  not not_315 (not_315_out, X2);
  not not_316 (not_316_out, X1);
  not not_317 (not_317_out, X4);
  not not_318 (not_318_out, X3);
  not not_319 (not_319_out, X1);
  not not_320 (not_320_out, Y3);
  not not_321 (not_321_out, X4);
  not not_322 (not_322_out, X3);
  not not_323 (not_323_out, X1);
  not not_324 (not_324_out, Y2);
  not not_325 (not_325_out, X4);
  not not_326 (not_326_out, X2);
  not not_327 (not_327_out, X1);
  not not_328 (not_328_out, Y3);
  not not_329 (not_329_out, X4);
  not not_330 (not_330_out, X1);
  not not_331 (not_331_out, Y4);
  not not_332 (not_332_out, X4);
  not not_333 (not_333_out, X1);
  not not_334 (not_334_out, Y3);
  not not_335 (not_335_out, Y2);
  not not_336 (not_336_out, X3);
  not not_337 (not_337_out, X2);
  not not_338 (not_338_out, X1);
  not not_339 (not_339_out, Y4);
  not not_340 (not_340_out, X3);
  not not_341 (not_341_out, X1);
  not not_342 (not_342_out, Y4);
  not not_343 (not_343_out, Y3);
  not not_344 (not_344_out, X3);
  not not_345 (not_345_out, X1);
  not not_346 (not_346_out, Y4);
  not not_347 (not_347_out, Y2);
  not not_348 (not_348_out, X2);
  not not_349 (not_349_out, X1);
  not not_350 (not_350_out, Y4);
  not not_351 (not_351_out, Y3);
  not not_352 (not_352_out, X1);
  not not_353 (not_353_out, Y4);
  not not_354 (not_354_out, Y3);
  not not_355 (not_355_out, Y2);
  not not_356 (not_356_out, X4);
  not not_357 (not_357_out, X3);
  not not_358 (not_358_out, X2);
  not not_359 (not_359_out, Y1);
  not not_360 (not_360_out, X4);
  not not_361 (not_361_out, X3);
  not not_362 (not_362_out, Y3);
  not not_363 (not_363_out, Y1);
  not not_364 (not_364_out, X4);
  not not_365 (not_365_out, X3);
  not not_366 (not_366_out, Y2);
  not not_367 (not_367_out, Y1);
  not not_368 (not_368_out, X4);
  not not_369 (not_369_out, X2);
  not not_370 (not_370_out, Y3);
  not not_371 (not_371_out, Y1);
  not not_372 (not_372_out, X4);
  not not_373 (not_373_out, Y4);
  not not_374 (not_374_out, Y1);
  not not_375 (not_375_out, X4);
  not not_376 (not_376_out, Y3);
  not not_377 (not_377_out, Y2);
  not not_378 (not_378_out, Y1);
  not not_379 (not_379_out, X3);
  not not_380 (not_380_out, X2);
  not not_381 (not_381_out, Y4);
  not not_382 (not_382_out, Y1);
  not not_383 (not_383_out, X3);
  not not_384 (not_384_out, Y4);
  not not_385 (not_385_out, Y3);
  not not_386 (not_386_out, Y1);
  not not_387 (not_387_out, X3);
  not not_388 (not_388_out, Y4);
  not not_389 (not_389_out, Y2);
  not not_390 (not_390_out, Y1);
  not not_391 (not_391_out, X2);
  not not_392 (not_392_out, Y4);
  not not_393 (not_393_out, Y3);
  not not_394 (not_394_out, Y1);
  not not_395 (not_395_out, Y4);
  not not_396 (not_396_out, Y3);
  not not_397 (not_397_out, Y2);
  not not_398 (not_398_out, Y1);
  and and_1 (and_1_out, X1, Y4, Y3, Y2, Y1);
  and and_2 (and_2_out, X2, Y4, Y3, Y2);
  and and_3 (and_3_out, X2, X1, Y4, Y3, Y1);
  and and_4 (and_4_out, X3, Y4, Y3);
  and and_5 (and_5_out, X3, X1, Y4, Y2, Y1);
  and and_6 (and_6_out, X3, X2, Y4, Y2);
  and and_7 (and_7_out, X3, X2, X1, Y4, Y1);
  and and_8 (and_8_out, X4, Y4);
  and and_9 (and_9_out, X4, X1, Y3, Y2, Y1);
  and and_10 (and_10_out, X4, X2, Y3, Y2);
  and and_11 (and_11_out, X4, X2, X1, Y3, Y1);
  and and_12 (and_12_out, X4, X3, Y3);
  and and_13 (and_13_out, X4, X3, X1, Y2, Y1);
  and and_14 (and_14_out, X4, X3, X2, Y2);
  and and_15 (and_15_out, X4, X3, X2, X1, Y1);
  and and_16 (and_16_out, not_1_out, not_2_out, not_3_out, not_4_out, Y4);
  and and_17 (and_17_out, not_5_out, not_6_out, not_7_out, Y4, not_8_out);
  and and_18 (and_18_out, not_9_out, not_10_out, not_11_out, Y4, not_12_out);
  and and_19 (and_19_out, not_13_out, not_14_out, not_15_out, Y4, not_16_out);
  and and_20 (and_20_out, not_17_out, not_18_out, Y4, not_19_out);
  and and_21 (and_21_out, not_20_out, not_21_out, Y4, not_22_out, not_23_out);
  and and_22 (and_22_out, not_24_out, not_25_out, not_26_out, Y4, not_27_out);
  and and_23 (and_23_out, not_28_out, not_29_out, Y4, not_30_out, not_31_out);
  and and_24 (and_24_out, not_32_out, not_33_out, Y4, not_34_out, not_35_out);
  and and_25 (and_25_out, not_36_out, not_37_out, Y4, not_38_out, not_39_out);
  and and_26 (and_26_out, not_40_out, Y4, not_41_out, not_42_out, not_43_out);
  and and_27 (and_27_out, not_44_out, X1, not_45_out, Y3, Y2, Y1);
  and and_28 (and_28_out, not_46_out, X2, not_47_out, Y3, Y2);
  and and_29 (and_29_out, not_48_out, X2, X1, not_49_out, Y3, Y1);
  and and_30 (and_30_out, not_50_out, X3, not_51_out, Y3);
  and and_31 (and_31_out, not_52_out, X3, X1, not_53_out, Y2, Y1);
  and and_32 (and_32_out, not_54_out, X3, X2, not_55_out, Y2);
  and and_33 (and_33_out, not_56_out, X3, X2, X1, not_57_out, Y1);
  and and_34 (and_34_out, X4, not_58_out, not_59_out, not_60_out, not_61_out);
  and and_35 (and_35_out, X4, not_62_out, not_63_out, not_64_out, not_65_out);
  and and_36 (and_36_out, X4, not_66_out, not_67_out, not_68_out, not_69_out);
  and and_37 (and_37_out, X4, not_70_out, not_71_out, not_72_out, not_73_out);
  and and_38 (and_38_out, X4, not_74_out, not_75_out, not_76_out);
  and and_39 (and_39_out, X4, not_77_out, not_78_out, not_79_out, not_80_out);
  and and_40 (and_40_out, X4, not_81_out, not_82_out, not_83_out, not_84_out);
  and and_41 (and_41_out, X4, not_85_out, not_86_out, not_87_out, not_88_out);
  and and_42 (and_42_out, X4, not_89_out, not_90_out, not_91_out, not_92_out);
  and and_43 (and_43_out, X4, not_93_out, not_94_out, not_95_out, not_96_out);
  and and_44 (and_44_out, X4, not_97_out, not_98_out, not_99_out, not_100_out);
  and and_45 (and_45_out, not_101_out, not_102_out, not_103_out, not_104_out, Y3);
  and and_46 (and_46_out, not_105_out, not_106_out, not_107_out, Y3, not_108_out);
  and and_47 (and_47_out, not_109_out, not_110_out, not_111_out, Y3, not_112_out);
  and and_48 (and_48_out, not_113_out, not_114_out, not_115_out, Y3, not_116_out);
  and and_49 (and_49_out, not_117_out, not_118_out, Y3, not_119_out, not_120_out);
  and and_50 (and_50_out, not_121_out, not_122_out, not_123_out, not_124_out, Y3);
  and and_51 (and_51_out, not_125_out, not_126_out, not_127_out, Y3, not_128_out);
  and and_52 (and_52_out, not_129_out, not_130_out, not_131_out, Y3, not_132_out);
  and and_53 (and_53_out, not_133_out, not_134_out, not_135_out, Y3, not_136_out);
  and and_54 (and_54_out, not_137_out, not_138_out, Y3, not_139_out, not_140_out);
  and and_55 (and_55_out, not_141_out, not_142_out, X1, not_143_out, Y2, Y1);
  and and_56 (and_56_out, not_144_out, X1, not_145_out, not_146_out, Y2, Y1);
  and and_57 (and_57_out, not_147_out, not_148_out, X2, not_149_out, Y2);
  and and_58 (and_58_out, not_150_out, X2, not_151_out, not_152_out, Y2);
  and and_59 (and_59_out, not_153_out, not_154_out, X2, X1, not_155_out, Y1);
  and and_60 (and_60_out, not_156_out, X2, X1, not_157_out, not_158_out, Y1);
  and and_61 (and_61_out, not_159_out, X3, not_160_out, not_161_out, not_162_out);
  and and_62 (and_62_out, not_163_out, X3, not_164_out, not_165_out, not_166_out);
  and and_63 (and_63_out, not_167_out, X3, not_168_out, not_169_out, not_170_out);
  and and_64 (and_64_out, not_171_out, X3, not_172_out, not_173_out, not_174_out);
  and and_65 (and_65_out, not_175_out, X3, not_176_out, not_177_out, not_178_out);
  and and_66 (and_66_out, X3, not_179_out, not_180_out, not_181_out, not_182_out);
  and and_67 (and_67_out, X3, not_183_out, not_184_out, not_185_out, not_186_out);
  and and_68 (and_68_out, X3, not_187_out, not_188_out, not_189_out, not_190_out);
  and and_69 (and_69_out, X3, not_191_out, not_192_out, not_193_out, not_194_out);
  and and_70 (and_70_out, X3, not_195_out, not_196_out, not_197_out, not_198_out);
  and and_71 (and_71_out, not_199_out, X3, X1, not_200_out, Y3, Y2, Y1);
  and and_72 (and_72_out, not_201_out, X3, X2, not_202_out, Y3, Y2);
  and and_73 (and_73_out, not_203_out, X3, X2, X1, not_204_out, Y3, Y1);
  and and_74 (and_74_out, not_205_out, not_206_out, not_207_out, not_208_out, Y2);
  and and_75 (and_75_out, not_209_out, not_210_out, not_211_out, Y2, not_212_out);
  and and_76 (and_76_out, not_213_out, not_214_out, not_215_out, not_216_out, Y2);
  and and_77 (and_77_out, not_217_out, not_218_out, not_219_out, not_220_out, Y2);
  and and_78 (and_78_out, not_221_out, not_222_out, not_223_out, Y2, not_224_out);
  and and_79 (and_79_out, not_225_out, not_226_out, not_227_out, Y2, not_228_out);
  and and_80 (and_80_out, not_229_out, not_230_out, not_231_out, not_232_out, Y2);
  and and_81 (and_81_out, not_233_out, not_234_out, not_235_out, Y2, not_236_out);
  and and_82 (and_82_out, not_237_out, not_238_out, not_239_out, not_240_out, Y2);
  and and_83 (and_83_out, not_241_out, not_242_out, not_243_out, Y2, not_244_out);
  and and_84 (and_84_out, not_245_out, not_246_out, not_247_out, X1, not_248_out, Y1);
  and and_85 (and_85_out, not_249_out, not_250_out, X1, not_251_out, not_252_out, Y1);
  and and_86 (and_86_out, not_253_out, not_254_out, X1, not_255_out, not_256_out, Y1);
  and and_87 (and_87_out, not_257_out, not_258_out, X1, not_259_out, not_260_out, Y1);
  and and_88 (and_88_out, not_261_out, X1, not_262_out, not_263_out, not_264_out, Y1);
  and and_89 (and_89_out, not_265_out, not_266_out, X2, not_267_out, not_268_out);
  and and_90 (and_90_out, not_269_out, not_270_out, X2, not_271_out, not_272_out);
  and and_91 (and_91_out, not_273_out, X2, not_274_out, not_275_out, not_276_out);
  and and_92 (and_92_out, not_277_out, X2, not_278_out, not_279_out, not_280_out);
  and and_93 (and_93_out, not_281_out, X2, not_282_out, not_283_out, not_284_out);
  and and_94 (and_94_out, not_285_out, X2, not_286_out, not_287_out, not_288_out);
  and and_95 (and_95_out, not_289_out, X2, not_290_out, not_291_out, not_292_out);
  and and_96 (and_96_out, not_293_out, X2, not_294_out, not_295_out, not_296_out);
  and and_97 (and_97_out, X2, not_297_out, not_298_out, not_299_out, not_300_out);
  and and_98 (and_98_out, X2, not_301_out, not_302_out, not_303_out, not_304_out);
  and and_99 (and_99_out, not_305_out, not_306_out, X2, X1, not_307_out, Y2, Y1);
  and and_100 (and_100_out, not_308_out, X2, X1, not_309_out, Y2, Y1);
  and and_101 (and_101_out, not_310_out, X2, X1, not_311_out, not_312_out, Y2, Y1);
  and and_102 (and_102_out, not_313_out, not_314_out, not_315_out, not_316_out, Y1);
  and and_103 (and_103_out, not_317_out, not_318_out, not_319_out, not_320_out, Y1);
  and and_104 (and_104_out, not_321_out, not_322_out, not_323_out, not_324_out, Y1);
  and and_105 (and_105_out, not_325_out, not_326_out, not_327_out, not_328_out, Y1);
  and and_106 (and_106_out, not_329_out, not_330_out, not_331_out, Y1);
  and and_107 (and_107_out, not_332_out, not_333_out, not_334_out, not_335_out, Y1);
  and and_108 (and_108_out, not_336_out, not_337_out, not_338_out, not_339_out, Y1);
  and and_109 (and_109_out, not_340_out, not_341_out, not_342_out, not_343_out, Y1);
  and and_110 (and_110_out, not_344_out, not_345_out, not_346_out, not_347_out, Y1);
  and and_111 (and_111_out, not_348_out, not_349_out, not_350_out, not_351_out, Y1);
  and and_112 (and_112_out, not_352_out, not_353_out, not_354_out, not_355_out, Y1);
  and and_113 (and_113_out, not_356_out, not_357_out, not_358_out, X1, not_359_out);
  and and_114 (and_114_out, not_360_out, not_361_out, X1, not_362_out, not_363_out);
  and and_115 (and_115_out, not_364_out, not_365_out, X1, not_366_out, not_367_out);
  and and_116 (and_116_out, not_368_out, not_369_out, X1, not_370_out, not_371_out);
  and and_117 (and_117_out, not_372_out, X1, not_373_out, not_374_out);
  and and_118 (and_118_out, not_375_out, X1, not_376_out, not_377_out, not_378_out);
  and and_119 (and_119_out, not_379_out, not_380_out, X1, not_381_out, not_382_out);
  and and_120 (and_120_out, not_383_out, X1, not_384_out, not_385_out, not_386_out);
  and and_121 (and_121_out, not_387_out, X1, not_388_out, not_389_out, not_390_out);
  and and_122 (and_122_out, not_391_out, X1, not_392_out, not_393_out, not_394_out);
  and and_123 (and_123_out, X1, not_395_out, not_396_out, not_397_out, not_398_out);
  or or_1 (ERRO, and_1_out, and_2_out, and_3_out, and_4_out, and_5_out, and_6_out, and_7_out, and_8_out, and_9_out, and_10_out, and_11_out, and_12_out, and_13_out, and_14_out, and_15_out);
  or or_2 (Z4, and_16_out, and_17_out, and_18_out, and_19_out, and_20_out, and_21_out, and_22_out, and_23_out, and_24_out, and_25_out, and_26_out, and_27_out, and_28_out, and_29_out, and_30_out, and_31_out, and_32_out, and_33_out, and_34_out, and_35_out, and_36_out, and_37_out, and_38_out, and_39_out, and_40_out, and_41_out, and_42_out, and_43_out, and_44_out);
  or or_3 (Z3, and_45_out, and_46_out, and_47_out, and_48_out, and_49_out, and_50_out, and_51_out, and_52_out, and_53_out, and_54_out, and_55_out, and_56_out, and_57_out, and_58_out, and_59_out, and_60_out, and_61_out, and_62_out, and_63_out, and_64_out, and_65_out, and_66_out, and_67_out, and_68_out, and_69_out, and_70_out, and_71_out, and_72_out, and_73_out);
  or or_4 (Z2, and_74_out, and_75_out, and_76_out, and_77_out, and_78_out, and_79_out, and_80_out, and_81_out, and_82_out, and_83_out, and_84_out, and_85_out, and_86_out, and_87_out, and_88_out, and_89_out, and_90_out, and_91_out, and_92_out, and_93_out, and_94_out, and_95_out, and_96_out, and_97_out, and_98_out, and_99_out, and_100_out, and_101_out);
  or or_5 (Z1, and_102_out, and_103_out, and_104_out, and_105_out, and_106_out, and_107_out, and_108_out, and_109_out, and_110_out, and_111_out, and_112_out, and_113_out, and_114_out, and_115_out, and_116_out, and_117_out, and_118_out, and_119_out, and_120_out, and_121_out, and_122_out, and_123_out);
endmodule

module calculador (
);

  operador operador_1 ();  // open: op1, op2, soma, subt, mult, divi
  soma soma_1 ();  // open: X4, X3, X2, X1, Y4, Y3, Y2, Y1, Z4, Z3, Z2, Z1, ERRO
endmodule

module operador (
  input  op1,
  input  op2,
  output soma,
  output subt,
  output mult,
  output divi
);

  wire not_1_out, not_2_out, not_3_out, not_4_out;

  not not_1 (not_1_out, op1);
  not not_2 (not_2_out, op2);
  not not_3 (not_3_out, op1);
  not not_4 (not_4_out, op2);
  and and_1 (divi, op1, op2);
  and and_2 (soma, not_1_out, not_2_out);
  and and_3 (subt, not_3_out, op2);
  and and_4 (mult, op1, not_4_out);
endmodule
