// Logisim project circuito.circ as structural Verilog: 15 circuits, main circuit main
module main (
  input  in_1,
  input  in_2,
  input  in_3,
  input  in_4,
  input  in_5,
  input  in_6,
  input  in_7,
  input  in_8,
  input  in_9,
  input  in_10,
  input  in_11,
  input  in_12,
  input  in_13,
  input  in_14,
  input  in_15,
  input  in_16,
  output A_B,
  output A_B_2,
  output A_B_3,
  output out_20
);

  wire undriven, undriven_2, undriven_3, undriven_4, undriven_5, undriven_6, undriven_7, undriven_8;
  wire [2:0] calculador_1_c;
  wire [3:0] conversor_hex_bin_1_x4, conversor_hex_bin_2_x4;
  wire [4:0] calculador_1_b;

  _7_Segment_Display u_7_segment_display_1 (
    .g(in_4), .f(in_2), .a(in_1), .b(in_3), .e(in_5), .d(in_9), .c(in_6));  // open: dp
  _7_Segment_Display u_7_segment_display_2 (
    .g(in_13), .f(in_11), .a(in_10), .b(in_12), .e(in_14), .d(in_16), .c(in_15));  // open: dp
  conversor_hex_bin conversor_hex_bin_1 (
    .a(in_1), .b(in_3), .c(in_6), .d(in_9), .e(in_5), .f(in_2), .g(in_4), .X4(conversor_hex_bin_1_x4[0]),
    .X3(conversor_hex_bin_1_x4[1]), .X2(conversor_hex_bin_1_x4[2]), .X1(conversor_hex_bin_1_x4[3]));
  conversor_hex_bin conversor_hex_bin_2 (
    .a(in_10), .b(in_12), .c(in_15), .d(in_16), .e(in_14), .f(in_11), .g(in_13),
    .X4(conversor_hex_bin_2_x4[0]), .X3(conversor_hex_bin_2_x4[1]), .X2(conversor_hex_bin_2_x4[2]),
    .X1(conversor_hex_bin_2_x4[3]));
  calculador calculador_1 (
    .A0(conversor_hex_bin_1_x4[3]), .A2(conversor_hex_bin_1_x4[1]), .A1(conversor_hex_bin_1_x4[2]),
    .A3(conversor_hex_bin_1_x4[0]), .B0(conversor_hex_bin_2_x4[3]), .B1(conversor_hex_bin_2_x4[2]),
    .B2(conversor_hex_bin_2_x4[1]), .B3(conversor_hex_bin_2_x4[0]), .op1(in_7), .op2(in_8), .A_B(A_B),
    .A_B_2(A_B_2), .A_B_3(A_B_3), .a(calculador_1_b[1]), .b(calculador_1_b[0]), .c(calculador_1_c[0]),
    .d(calculador_1_c[1]), .e(calculador_1_c[2]), .f(calculador_1_b[2]), .g(calculador_1_b[3]),
    .erro(out_20), .neg(calculador_1_b[4]));
  _7_Segment_Display u_7_segment_display_3 (
    .g(calculador_1_b[3]), .f(calculador_1_b[2]), .a(calculador_1_b[1]), .b(calculador_1_b[0]),
    .e(calculador_1_c[2]), .d(calculador_1_c[1]), .c(calculador_1_c[0]), .dp(undriven_8));
  _7_Segment_Display u_7_segment_display_4 (
    .g(calculador_1_b[4]), .f(undriven_2), .a(undriven_4), .b(undriven_6), .e(undriven), .d(undriven_3),
    .c(undriven_5), .dp(undriven_7));

  // Other names for the same wires on the sheet: Erro = out_20

  // Notes on the sheet:
  //   PROJETO ---------------------------------------------------
  //   CALCULADORA HEXADECIMAL
  //   ---------------------------------------------------------------------
  //   SELETOR DA OPERAÇÃO
  //   00 - Soma                01 - Subtração
  //   10 - Multiplicação   11 - Comparação (maior)
  //   RESULTADO
  //   👆 Resultado é maior que F.
  //   Comparação (maior):
  //   Ciência da Computação 2024.1
  //   Circuitos Digitais - Prof. Ramon Nepomuceno
  //   Eduardo Pereira da Sousa Filho
  //   Sebastião Sousa Soares
endmodule

module conversor_hex_bin (
  input  a,
  input  b,
  input  c,
  input  d,
  input  e,
  input  f,
  input  g,
  output X4,
  output X3,
  output X2,
  output X1
);

  wire and_1_out, and_2_out, and_3_out, and_4_out, and_5_out, and_6_out, and_7_out, and_8_out, and_9_out,
       and_10_out, and_11_out, and_12_out, and_13_out, and_14_out, and_15_out, and_16_out, and_17_out,
       and_18_out, and_19_out, and_20_out, and_21_out, and_22_out, and_23_out, and_24_out, not_1_out,
       not_2_out, not_3_out, not_4_out, not_5_out, not_6_out, not_7_out, not_8_out, not_9_out, not_10_out,
       not_11_out, not_12_out, not_13_out, not_14_out, not_15_out, not_16_out, not_17_out, not_18_out,
       not_19_out, not_20_out, not_21_out, not_22_out, not_23_out, not_24_out, not_25_out, not_26_out,
       not_27_out, not_28_out, not_29_out, not_30_out, not_31_out, not_32_out, not_33_out, not_34_out,
       not_35_out, not_36_out, not_37_out, not_38_out, not_39_out, not_40_out, not_41_out, not_42_out,
       not_43_out, not_44_out, not_45_out, not_46_out, not_47_out;

  not not_1 (not_1_out, a);
  not not_2 (not_2_out, b);
  not not_3 (not_3_out, a);
  not not_4 (not_4_out, f);
  not not_5 (not_5_out, b);
  not not_6 (not_6_out, c);
  not not_7 (not_7_out, b);
  not not_8 (not_8_out, c);
  not not_9 (not_9_out, a);
  not not_10 (not_10_out, d);
  not not_11 (not_11_out, e);
  not not_12 (not_12_out, a);
  not not_13 (not_13_out, f);
  not not_14 (not_14_out, b);
  not not_15 (not_15_out, c);
  not not_16 (not_16_out, b);
  not not_17 (not_17_out, c);
  not not_18 (not_18_out, b);
  not not_19 (not_19_out, d);
  not not_20 (not_20_out, e);
  not not_21 (not_21_out, f);
  not not_22 (not_22_out, g);
  not not_23 (not_23_out, b);
  not not_24 (not_24_out, b);
  not not_25 (not_25_out, c);
  not not_26 (not_26_out, c);
  not not_27 (not_27_out, f);
  not not_28 (not_28_out, d);
  not not_29 (not_29_out, e);
  not not_30 (not_30_out, f);
  not not_31 (not_31_out, g);
  not not_32 (not_32_out, d);
  not not_33 (not_33_out, e);
  not not_34 (not_34_out, f);
  not not_35 (not_35_out, a);
  not not_36 (not_36_out, b);
  not not_37 (not_37_out, d);
  not not_38 (not_38_out, e);
  not not_39 (not_39_out, f);
  not not_40 (not_40_out, g);
  not not_41 (not_41_out, a);
  not not_42 (not_42_out, f);
  not not_43 (not_43_out, b);
  not not_44 (not_44_out, c);
  not not_45 (not_45_out, d);
  not not_46 (not_46_out, e);
  not not_47 (not_47_out, e);
  and and_1 (and_1_out, not_1_out, not_2_out, c, d, e, f, g);
  and and_2 (and_2_out, not_3_out, b, c, d, e, not_4_out, g);
  and and_3 (and_3_out, a, not_5_out, not_6_out, e, f, g);
  and and_4 (and_4_out, a, not_7_out, not_8_out, d, e, f);
  and and_5 (and_5_out, a, b, c, e, f, g);
  and and_6 (and_6_out, a, b, c, d, f, g);
  and and_7 (and_7_out, not_9_out, b, c, not_10_out, not_11_out, f, g);
  and and_8 (and_8_out, not_12_out, b, c, d, e, not_13_out, g);
  and and_9 (and_9_out, a, not_14_out, not_15_out, e, f, g);
  and and_10 (and_10_out, a, not_16_out, not_17_out, d, e, f);
  and and_11 (and_11_out, a, not_18_out, c, d, f, g);
  and and_12 (and_12_out, a, b, c, not_19_out, not_20_out, not_21_out, not_22_out);
  and and_13 (and_13_out, not_23_out, c, d, e, f, g);
  and and_14 (and_14_out, a, not_24_out, not_25_out, e, f, g);
  and and_15 (and_15_out, a, b, not_26_out, d, e, not_27_out, g);
  and and_16 (and_16_out, a, b, c, not_28_out, not_29_out, not_30_out, not_31_out);
  and and_17 (and_17_out, a, b, c, not_32_out, e, f, g);
  and and_18 (and_18_out, a, b, c, d, not_33_out, not_34_out, g);
  and and_19 (and_19_out, not_35_out, not_36_out, c, d, e, f, g);
  and and_20 (and_20_out, b, c, not_37_out, not_38_out, not_39_out, not_40_out);
  and and_21 (and_21_out, not_41_out, b, c, d, e, not_42_out, g);
  and and_22 (and_22_out, a, not_43_out, not_44_out, not_45_out, e, f, g);
  and and_23 (and_23_out, a, c, d, not_46_out, f, g);
  and and_24 (and_24_out, a, b, c, d, not_47_out, g);
  or or_1 (X4, and_1_out, and_2_out, and_3_out, and_4_out, and_5_out, and_6_out);
  or or_2 (X3, and_7_out, and_8_out, and_9_out, and_10_out, and_11_out, and_12_out);
  or or_3 (X2, and_13_out, and_14_out, and_15_out, and_16_out, and_17_out, and_18_out);
  or or_4 (X1, and_19_out, and_20_out, and_21_out, and_22_out, and_23_out, and_24_out);
endmodule

module conversor_bin_hex (
  input  X4,
  input  X3,
  input  X2,
  input  X1,
  output a,
  output b,
  output c,
  output d,
  output e,
  output f,
  output g
);

  wire and_1_out, and_2_out, and_3_out, and_4_out, and_5_out, and_6_out, and_7_out, and_8_out, and_9_out,
       and_10_out, and_11_out, and_12_out, and_13_out, and_14_out, and_15_out, and_16_out, and_17_out,
       and_18_out, and_19_out, and_20_out, and_21_out, and_22_out, and_23_out, and_24_out, and_25_out,
       and_26_out, and_27_out, and_28_out, and_29_out, and_30_out, and_31_out, and_32_out, and_33_out,
       and_34_out, and_35_out, not_1_out, not_2_out, not_3_out, not_4_out, not_5_out, not_6_out, not_7_out,
       not_8_out, not_9_out, not_10_out, not_11_out, not_12_out, not_13_out, not_14_out, not_15_out,
       not_16_out, not_17_out, not_18_out, not_19_out, not_20_out, not_21_out, not_22_out, not_23_out,
       not_24_out, not_25_out, not_26_out, not_27_out, not_28_out, not_29_out, not_30_out, not_31_out,
       not_32_out, not_33_out, not_34_out, not_35_out, not_36_out, not_37_out, not_38_out, not_39_out,
       not_40_out, not_41_out, not_42_out, not_43_out;

  not not_1 (not_1_out, X3);
  and and_1 (and_1_out, not_1_out, not_2_out);
  not not_2 (not_2_out, X1);
  not not_3 (not_3_out, X4);
  and and_2 (and_2_out, not_3_out, X2);
  not not_4 (not_4_out, X4);
  and and_3 (and_3_out, not_4_out, X3, X1);
  and and_4 (and_4_out, X3, X2);
  and and_5 (and_5_out, X4, not_5_out, not_6_out);
  not not_5 (not_5_out, X3);
  not not_6 (not_6_out, X2);
  and and_6 (and_6_out, X4, not_7_out);
  not not_7 (not_7_out, X1);
  not not_8 (not_8_out, X4);
  and and_7 (and_7_out, not_8_out, not_9_out);
  not not_9 (not_9_out, X3);
  not not_10 (not_10_out, X4);
  not not_11 (not_11_out, X2);
  and and_8 (and_8_out, not_10_out, not_11_out, not_12_out);
  not not_12 (not_12_out, X1);
  not not_13 (not_13_out, X3);
  and and_9 (and_9_out, not_13_out, not_14_out);
  not not_14 (not_14_out, X1);
  not not_15 (not_15_out, X4);
  and and_10 (and_10_out, not_15_out, X2, X1);
  not not_16 (not_16_out, X2);
  and and_11 (and_11_out, X4, not_16_out, X1);
  not not_17 (not_17_out, X4);
  and and_12 (and_12_out, not_17_out, not_18_out);
  not not_18 (not_18_out, X2);
  not not_19 (not_19_out, X4);
  and and_13 (and_13_out, not_19_out, X1);
  not not_20 (not_20_out, X2);
  and and_14 (and_14_out, not_20_out, X1);
  not not_21 (not_21_out, X4);
  and and_15 (and_15_out, not_21_out, X3);
  and and_16 (and_16_out, X4, not_22_out);
  not not_22 (not_22_out, X3);
  not not_23 (not_23_out, X4);
  not not_24 (not_24_out, X3);
  and and_17 (and_17_out, not_23_out, not_24_out, not_25_out);
  not not_25 (not_25_out, X1);
  not not_26 (not_26_out, X3);
  and and_18 (and_18_out, not_26_out, X2, X1);
  and and_19 (and_19_out, X3, not_27_out, X1);
  not not_27 (not_27_out, X2);
  and and_20 (and_20_out, X3, X2, not_28_out);
  not not_28 (not_28_out, X1);
  and and_21 (and_21_out, X4, not_29_out);
  not not_29 (not_29_out, X2);
  not not_30 (not_30_out, X3);
  and and_22 (and_22_out, not_30_out, not_31_out);
  not not_31 (not_31_out, X1);
  and and_23 (and_23_out, X2, not_32_out);
  not not_32 (not_32_out, X1);
  and and_24 (and_24_out, X4, X2);
  and and_25 (and_25_out, X4, X3);
  not not_33 (not_33_out, X2);
  and and_26 (and_26_out, not_33_out, not_34_out);
  not not_34 (not_34_out, X1);
  not not_35 (not_35_out, X4);
  and and_27 (and_27_out, not_35_out, X3, not_36_out);
  not not_36 (not_36_out, X2);
  and and_28 (and_28_out, X3, not_37_out);
  not not_37 (not_37_out, X1);
  and and_29 (and_29_out, X4, not_38_out);
  not not_38 (not_38_out, X3);
  and and_30 (and_30_out, X4, X2);
  not not_39 (not_39_out, X3);
  and and_31 (and_31_out, not_39_out, X2);
  and and_32 (and_32_out, X2, not_40_out);
  not not_40 (not_40_out, X1);
  not not_41 (not_41_out, X4);
  and and_33 (and_33_out, not_41_out, X3, not_42_out);
  not not_42 (not_42_out, X2);
  and and_34 (and_34_out, X4, not_43_out);
  not not_43 (not_43_out, X3);
  and and_35 (and_35_out, X4, X1);
  or or_1 (b, and_7_out, and_8_out, and_9_out, and_10_out, and_11_out);
  or or_2 (c, and_12_out, and_13_out, and_14_out, and_15_out, and_16_out);
  or or_3 (d, and_17_out, and_18_out, and_19_out, and_20_out, and_21_out);
  or or_4 (e, and_22_out, and_23_out, and_24_out, and_25_out);
  or or_5 (f, and_26_out, and_27_out, and_28_out, and_29_out, and_30_out);
  or or_6 (g, and_31_out, and_32_out, and_33_out, and_34_out, and_35_out);
  or or_7 (a, and_1_out, and_2_out, and_3_out, and_4_out, and_5_out, and_6_out);
endmodule

module calculador (
  input  A3,
  input  A2,
  input  A1,
  input  A0,
  input  B3,
  input  B2,
  input  B1,
  input  B0,
  input  op1,
  input  op2,
  output a,
  output b,
  output c,
  output d,
  output e,
  output f,
  output g,
  output neg,
  output A_B,
  output A_B_2,
  output A_B_3,
  output erro
);

  wire and_2_out, and_3_out, and_5_out, and_8_out, and_9_out, and_10_out, conversor_bin_hex_1_a,
       conversor_bin_hex_1_b, conversor_bin_hex_1_c, conversor_bin_hex_1_d, conversor_bin_hex_1_e,
       conversor_bin_hex_1_f, conversor_bin_hex_1_g, maior_2x4bits_1_difout, maior_2x4bits_1_m0,
       maior_2x4bits_1_m1, maior_2x4bits_1_m2, maior_2x4bits_1_m3, maior_2x4bits_1_posout,
       multiplicador_1_erro, multiplicador_1_r0, multiplicador_1_r1, multiplicador_1_r2, multiplicador_1_r3,
       mux_4x4bits_1_s1, mux_4x4bits_1_s2, mux_4x4bits_1_s3, mux_4x4bits_1_s4, not_1_out,
       somador2x4bits_1_co, somador2x4bits_1_s0, somador2x4bits_1_s1, somador2x4bits_1_s2,
       somador2x4bits_1_s3, subtrator_1_negout, subtrator_1_s0, subtrator_1_s1, subtrator_1_s2,
       subtrator_1_s3;

  somador2x4bits somador2x4bits_1 (
    .ci(1'b0), .a0(A0), .b0(B0), .a1(A1), .b1(B1), .a2(A2), .b2(B2), .a3(A3), .b3(B3),
    .s0(somador2x4bits_1_s0), .s1(somador2x4bits_1_s1), .s2(somador2x4bits_1_s2), .s3(somador2x4bits_1_s3),
    .co(somador2x4bits_1_co));
  subtrator subtrator_1 (
    .a0(A0), .a1(A1), .a2(A2), .a3(A3), .b0(B0), .b1(B1), .b2(B2), .b3(B3), .in_1(1'b0), .s0(subtrator_1_s0),
    .s1(subtrator_1_s1), .s2(subtrator_1_s2), .s3(subtrator_1_s3), .negOut(subtrator_1_negout));
  multiplicador multiplicador_1 (
    .a2(A3), .b3(B3), .r3(multiplicador_1_r3), .a2_2(A2), .b2(B2), .r2(multiplicador_1_r2), .a1(A1), .b1(B1),
    .r1(multiplicador_1_r1), .a0(A0), .b0(B0), .r0(multiplicador_1_r0), .erro(multiplicador_1_erro));
  maior_2x4bits maior_2x4bits_1 (
    .a3(A3), .b3(B3), .a2(A2), .b2(B2), .a1(A1), .b1(B1), .a0(A0), .b0(B0), .m3(maior_2x4bits_1_m3),
    .m2(maior_2x4bits_1_m2), .m1(maior_2x4bits_1_m1), .m0(maior_2x4bits_1_m0),
    .posOut(maior_2x4bits_1_posout), .difOut(maior_2x4bits_1_difout));
  mux_4x4bits mux_4x4bits_1 (
    .ra1(somador2x4bits_1_s0), .rb1(subtrator_1_s0), .rc1(multiplicador_1_r0), .rd1(maior_2x4bits_1_m0),
    .ra2(somador2x4bits_1_s1), .rb2(subtrator_1_s1), .rc2(multiplicador_1_r1), .rd2(maior_2x4bits_1_m1),
    .ra3(somador2x4bits_1_s2), .rb3(subtrator_1_s2), .rc3(multiplicador_1_r2), .rd3(maior_2x4bits_1_m2),
    .ra4(somador2x4bits_1_s3), .rb4(subtrator_1_s3), .rc4(multiplicador_1_r3), .rd4(maior_2x4bits_1_m3),
    .op1(op1), .op2(op2), .S4(mux_4x4bits_1_s4), .S3(mux_4x4bits_1_s3), .S2(mux_4x4bits_1_s2),
    .S1(mux_4x4bits_1_s1));
  conversor_bin_hex conversor_bin_hex_1 (
    .X4(mux_4x4bits_1_s4), .X3(mux_4x4bits_1_s3), .X2(mux_4x4bits_1_s2), .X1(mux_4x4bits_1_s1),
    .a(conversor_bin_hex_1_a), .b(conversor_bin_hex_1_b), .c(conversor_bin_hex_1_c),
    .d(conversor_bin_hex_1_d), .e(conversor_bin_hex_1_e), .f(conversor_bin_hex_1_f), .g(conversor_bin_hex_1_g));
  tratador_de_erro tratador_de_erro_1 (
    .erro(erro), .a(conversor_bin_hex_1_a), .b(conversor_bin_hex_1_b), .c(conversor_bin_hex_1_c),
    .d(conversor_bin_hex_1_d), .e(conversor_bin_hex_1_e), .f(conversor_bin_hex_1_f),
    .g(conversor_bin_hex_1_g), .a2(a), .b2(b), .c2(c), .d2(d), .e2(e), .f2(f), .g2(g));
  and and_1 (neg, subtrator_1_negout, and_2_out);
  and and_2 (and_2_out, ~op1, op2);  // AND_Gate
  and and_3 (and_3_out, op1, op2);
  and and_4 (A_B, and_3_out, and_5_out);
  and and_5 (and_5_out, maior_2x4bits_1_difout, ~maior_2x4bits_1_posout);  // AND_Gate
  and and_6 (A_B_2, and_3_out, not_1_out);
  not not_1 (not_1_out, maior_2x4bits_1_difout);
  and and_7 (A_B_3, and_3_out, and_8_out);
  and and_8 (and_8_out, maior_2x4bits_1_difout, maior_2x4bits_1_posout);
  and and_9 (and_9_out, somador2x4bits_1_co, ~op2, ~op1);  // AND_Gate
  or or_1 (erro, and_9_out, and_10_out);
  and and_10 (and_10_out, multiplicador_1_erro, ~op2, op1);  // AND_Gate

  // Other names for the same wires on the sheet: A_t[3:0] = {A3, A2, A1, A0}; B_t[3:0] = {B3, B2, B1, B0};
  //   op[1:0] = {op2, op1}
endmodule

module mux_4x1bit (
  input  op1,
  input  op2,
  input  ra,
  input  rb,
  input  rc,
  input  rd,
  output out_7
);

  wire and_1_out, and_2_out, and_3_out, and_4_out, and_5_out, and_6_out, and_7_out, and_8_out;

  and and_1 (and_1_out, op2, op1);
  and and_2 (and_2_out, ~op2, ~op1);  // AND_Gate
  and and_3 (and_3_out, op2, ~op1);  // AND_Gate
  and and_4 (and_4_out, ~op2, op1);  // AND_Gate
  and and_5 (and_5_out, and_2_out, ra);
  and and_6 (and_6_out, and_3_out, rb);
  and and_7 (and_7_out, and_4_out, rc);
  and and_8 (and_8_out, and_1_out, rd);
  or or_1 (out_7, and_5_out, and_6_out, and_7_out, and_8_out);
endmodule

module mux_4x4bits (
  input  op1,
  input  op2,
  input  ra1,
  input  rb1,
  input  rc1,
  input  rd1,
  input  ra2,
  input  rb2,
  input  rc2,
  input  rd2,
  input  ra3,
  input  rb3,
  input  rc3,
  input  rd3,
  input  ra4,
  input  rb4,
  input  rc4,
  input  rd4,
  output S4,
  output S3,
  output S2,
  output S1
);

  mux_4x1bit mux_4x1bit_1 (.op1(op1), .op2(op2), .ra(ra1), .rb(rb1), .rc(rc1), .out_7(S1), .rd(rd1));
  mux_4x1bit mux_4x1bit_2 (.op1(op1), .op2(op2), .ra(ra2), .rb(rb2), .rc(rc2), .out_7(S2), .rd(rd2));
  mux_4x1bit mux_4x1bit_3 (.op1(op1), .op2(op2), .ra(ra3), .rb(rb3), .rc(rc3), .out_7(S3), .rd(rd3));
  mux_4x1bit mux_4x1bit_4 (.op1(op1), .op2(op2), .ra(ra4), .rb(rb4), .rc(rc4), .out_7(S4), .rd(rd4));
endmodule

module meio_somador (
  input  a,
  input  b,
  output S,
  output c0
);

  xor xor_1 (S, a, b);
  and and_1 (c0, a, b);
endmodule

module somador_inteiro (
  input  ci,
  input  a,
  input  b,
  output S,
  output co
);

  wire meio_somador_1_c0, meio_somador_1_s, meio_somador_2_c0;

  meio_somador meio_somador_1 (.a(a), .b(b), .S(meio_somador_1_s), .c0(meio_somador_1_c0));
  meio_somador meio_somador_2 (.a(ci), .b(meio_somador_1_s), .S(S), .c0(meio_somador_2_c0));
  or or_1 (co, meio_somador_2_c0, meio_somador_1_c0);
endmodule

module somador2x4bits (
  input  ci,
  input  a0,
  input  b0,
  input  a1,
  input  b1,
  input  a2,
  input  b2,
  input  a3,
  input  b3,
  output s0,
  output s1,
  output s2,
  output s3,
  output co
);

  wire somador_inteiro_1_co, somador_inteiro_2_co, somador_inteiro_3_co;

  somador_inteiro somador_inteiro_1 (.ci(ci), .a(a0), .b(b0), .S(s0), .co(somador_inteiro_1_co));
  somador_inteiro somador_inteiro_2 (.ci(somador_inteiro_1_co), .a(a1), .b(b1), .S(s1), .co(somador_inteiro_2_co));
  somador_inteiro somador_inteiro_3 (.ci(somador_inteiro_2_co), .a(a2), .b(b2), .S(s2), .co(somador_inteiro_3_co));
  somador_inteiro somador_inteiro_4 (.ci(somador_inteiro_3_co), .a(a3), .b(b3), .S(s3), .co(co));
endmodule

module cpl2 (
  input  a0,
  input  a1,
  input  a2,
  input  a3,
  output x0,
  output x1,
  output x2,
  output x3,
  output x
);

  wire not_1_out, not_2_out, not_3_out, not_4_out;

  not not_1 (not_1_out, a0);
  not not_2 (not_2_out, a1);
  not not_3 (not_3_out, a2);
  not not_4 (not_4_out, a3);
  somador2x4bits somador2x4bits_1 (
    .ci(1'b0), .a0(not_1_out), .b0(1'b1), .a1(not_2_out), .b1(1'b0), .a2(not_3_out), .b2(1'b0),
    .a3(not_4_out), .b3(1'b0), .s0(x0), .s1(x1), .s2(x2), .s3(x3), .co(x));
endmodule

module subtrator (
  input  in_1,
  input  a0,
  input  a1,
  input  a2,
  input  a3,
  input  b0,
  input  b1,
  input  b2,
  input  b3,
  output s0,
  output s1,
  output s2,
  output s3,
  output negOut
);

  wire and_1_out, and_2_out, and_3_out, and_4_out, and_5_out, and_6_out, and_7_out, and_8_out, cpl2_1_x0,
       cpl2_1_x1, cpl2_1_x2, cpl2_1_x3, cpl2_2_x0, cpl2_2_x1, cpl2_2_x2, cpl2_2_x3, somador2x4bits_1_s0,
       somador2x4bits_1_s1, somador2x4bits_1_s2, somador2x4bits_1_s3;

  maior_2x4bits maior_2x4bits_1 (
    .a3(a3), .b3(b3), .a2(a2), .b2(b2), .a1(a1), .b1(b1), .a0(a0), .b0(b0), .posOut(negOut));  // open: m3, m2, m1, m0, difOut
  cpl2 cpl2_1 (
    .a0(b0), .a1(b1), .a2(b2), .a3(b3), .x0(cpl2_1_x0), .x1(cpl2_1_x1), .x2(cpl2_1_x2), .x3(cpl2_1_x3));  // open: x
  somador2x4bits somador2x4bits_1 (
    .ci(in_1), .a0(a0), .b0(cpl2_1_x0), .a1(a1), .b1(cpl2_1_x1), .a2(a2), .b2(cpl2_1_x2), .a3(a3),
    .b3(cpl2_1_x3), .s0(somador2x4bits_1_s0), .s1(somador2x4bits_1_s1), .s2(somador2x4bits_1_s2),
    .s3(somador2x4bits_1_s3));  // open: co
  cpl2 cpl2_2 (
    .a0(somador2x4bits_1_s0), .a1(somador2x4bits_1_s1), .a2(somador2x4bits_1_s2), .a3(somador2x4bits_1_s3),
    .x0(cpl2_2_x0), .x1(cpl2_2_x1), .x2(cpl2_2_x2), .x3(cpl2_2_x3));  // open: x
  and and_1 (and_1_out, ~negOut, somador2x4bits_1_s0);  // AND_Gate
  and and_2 (and_2_out, negOut, cpl2_2_x0);
  and and_3 (and_3_out, ~negOut, somador2x4bits_1_s1);  // AND_Gate
  and and_4 (and_4_out, negOut, cpl2_2_x1);
  and and_5 (and_5_out, ~negOut, somador2x4bits_1_s2);  // AND_Gate
  and and_6 (and_6_out, negOut, cpl2_2_x2);
  and and_7 (and_7_out, ~negOut, somador2x4bits_1_s3);  // AND_Gate
  and and_8 (and_8_out, negOut, cpl2_2_x3);
  or or_1 (s0, and_1_out, and_2_out);
  or or_2 (s1, and_3_out, and_4_out);
  or or_3 (s2, and_5_out, and_6_out);
  or or_4 (s3, and_7_out, and_8_out);
endmodule

module maior_2x1bit (
  input  a,
  input  b,
  input  posIn,
  input  difIn,
  output x,
  output posOut,
  output difOut
);

  wire and_1_out, and_2_out, and_3_out, and_4_out, and_5_out, and_6_out, and_7_out, and_8_out, and_9_out,
       and_10_out, not_1_out, not_2_out, not_3_out, not_4_out, not_5_out, not_6_out, not_7_out, not_8_out;

  and and_1 (and_1_out, b, not_1_out);
  not not_1 (not_1_out, difIn);
  and and_2 (and_2_out, b, posIn);
  and and_3 (and_3_out, a, not_2_out);
  not not_2 (not_2_out, posIn);
  and and_4 (and_4_out, a, not_3_out);
  not not_3 (not_3_out, difIn);
  not not_4 (not_4_out, a);
  and and_5 (and_5_out, not_4_out, posIn);
  and and_6 (and_6_out, posIn, difIn);
  not not_5 (not_5_out, a);
  and and_7 (and_7_out, not_5_out, b, not_6_out);
  not not_6 (not_6_out, difIn);
  and and_8 (and_8_out, b, posIn);
  not not_7 (not_7_out, a);
  and and_9 (and_9_out, not_7_out, b);
  and and_10 (and_10_out, a, not_8_out);
  not not_8 (not_8_out, b);
  or or_1 (x, and_1_out, and_2_out, and_3_out, and_4_out);
  or or_2 (posOut, and_5_out, and_6_out, and_7_out, and_8_out);
  or or_3 (difOut, difIn, and_9_out, and_10_out);
endmodule

module maior_2x4bits (
  input  a3,
  input  a2,
  input  a1,
  input  a0,
  input  b3,
  input  b2,
  input  b1,
  input  b0,
  output m3,
  output m2,
  output m1,
  output m0,
  output posOut,
  output difOut
);

  wire maior_2x1bit_1_difout, maior_2x1bit_1_posout, maior_2x1bit_2_difout, maior_2x1bit_2_posout,
       maior_2x1bit_3_difout, maior_2x1bit_3_posout;

  maior_2x1bit maior_2x1bit_1 (
    .a(a3), .b(b3), .posIn(1'b0), .difIn(1'b0), .x(m3), .posOut(maior_2x1bit_1_posout),
    .difOut(maior_2x1bit_1_difout));
  maior_2x1bit maior_2x1bit_2 (
    .a(a2), .b(b2), .posIn(maior_2x1bit_1_posout), .difIn(maior_2x1bit_1_difout), .x(m2),
    .posOut(maior_2x1bit_2_posout), .difOut(maior_2x1bit_2_difout));
  maior_2x1bit maior_2x1bit_3 (
    .a(a1), .b(b1), .posIn(maior_2x1bit_2_posout), .difIn(maior_2x1bit_2_difout), .x(m1),
    .posOut(maior_2x1bit_3_posout), .difOut(maior_2x1bit_3_difout));
  maior_2x1bit maior_2x1bit_4 (
    .a(a0), .b(b0), .posIn(maior_2x1bit_3_posout), .difIn(maior_2x1bit_3_difout), .x(m0), .posOut(posOut),
    .difOut(difOut));
endmodule

module multiplicador (
  input  a2,
  input  a2_2,
  input  a1,
  input  a0,
  input  b3,
  input  b2,
  input  b1,
  input  b0,
  output r3,
  output r2,
  output r1,
  output r0,
  output erro
);

  wire and_1_out, and_2_out, and_3_out, and_4_out, and_5_out, and_6_out, and_7_out, and_8_out, and_9_out,
       and_10_out, and_11_out, and_12_out, and_13_out, and_14_out, and_15_out, meio_somador_1_c0,
       meio_somador_2_c0, meio_somador_3_c0, somador_inteiro_1_co, somador_inteiro_1_s, somador_inteiro_2_co,
       somador_inteiro_2_s, somador_inteiro_3_co, somador_inteiro_3_s, somador_inteiro_4_co,
       somador_inteiro_4_s, somador_inteiro_5_co, somador_inteiro_5_s, somador_inteiro_6_co,
       somador_inteiro_6_s, somador_inteiro_7_co, somador_inteiro_7_s, somador_inteiro_8_co,
       somador_inteiro_8_s, somador_inteiro_9_co, somador_inteiro_9_s;

  and and_1 (and_1_out, b3, a2);
  somador_inteiro somador_inteiro_1 (
    .ci(somador_inteiro_3_co), .a(somador_inteiro_2_co), .b(and_1_out), .S(somador_inteiro_1_s),
    .co(somador_inteiro_1_co));
  and and_2 (and_2_out, b3, a1);
  and and_3 (and_3_out, b3, a2_2);
  somador_inteiro somador_inteiro_2 (
    .ci(somador_inteiro_5_co), .a(somador_inteiro_4_co), .b(and_3_out), .S(somador_inteiro_2_s),
    .co(somador_inteiro_2_co));
  and and_4 (and_4_out, b2, a2);
  somador_inteiro somador_inteiro_3 (
    .ci(somador_inteiro_6_co), .a(somador_inteiro_2_s), .b(and_4_out), .S(somador_inteiro_3_s),
    .co(somador_inteiro_3_co));
  or or_1 (erro, somador_inteiro_1_co, somador_inteiro_1_s, somador_inteiro_3_s, somador_inteiro_6_s);
  and and_5 (and_5_out, b2, a1);
  somador_inteiro somador_inteiro_4 (
    .ci(somador_inteiro_7_co), .a(1'b0), .b(and_2_out), .S(somador_inteiro_4_s), .co(somador_inteiro_4_co));
  and and_6 (and_6_out, b2, a2_2);
  somador_inteiro somador_inteiro_5 (
    .ci(somador_inteiro_8_co), .a(somador_inteiro_4_s), .b(and_6_out), .S(somador_inteiro_5_s),
    .co(somador_inteiro_5_co));
  and and_7 (and_7_out, b1, a2);
  somador_inteiro somador_inteiro_6 (
    .ci(meio_somador_1_c0), .a(somador_inteiro_5_s), .b(and_7_out), .S(somador_inteiro_6_s),
    .co(somador_inteiro_6_co));
  and and_8 (and_8_out, b3, a0);
  and and_9 (and_9_out, b1, a1);
  somador_inteiro somador_inteiro_7 (
    .ci(somador_inteiro_9_co), .a(and_8_out), .b(and_5_out), .S(somador_inteiro_7_s),
    .co(somador_inteiro_7_co));
  and and_10 (and_10_out, b1, a2_2);
  somador_inteiro somador_inteiro_8 (
    .ci(meio_somador_2_c0), .a(somador_inteiro_7_s), .b(and_10_out), .S(somador_inteiro_8_s),
    .co(somador_inteiro_8_co));
  and and_11 (and_11_out, b0, a2);
  meio_somador meio_somador_1 (.a(somador_inteiro_8_s), .b(and_11_out), .S(r3), .c0(meio_somador_1_c0));
  and and_12 (and_12_out, b2, a0);
  and and_13 (and_13_out, b0, a1);
  somador_inteiro somador_inteiro_9 (
    .ci(meio_somador_3_c0), .a(and_12_out), .b(and_9_out), .S(somador_inteiro_9_s), .co(somador_inteiro_9_co));
  and and_14 (and_14_out, b0, a2_2);
  meio_somador meio_somador_2 (.a(somador_inteiro_9_s), .b(and_14_out), .S(r2), .c0(meio_somador_2_c0));
  and and_15 (and_15_out, b1, a0);
  meio_somador meio_somador_3 (.a(and_15_out), .b(and_13_out), .S(r1), .c0(meio_somador_3_c0));
  and and_16 (r0, b0, a0);

  // Other names for the same wires on the sheet: a2_t = a2_2; a3 = a2
endmodule

module tratador_de_erro (
  input  erro,
  input  a,
  input  b,
  input  c,
  input  d,
  input  e,
  input  f,
  input  g,
  output a2,
  output b2,
  output c2,
  output d2,
  output e2,
  output f2,
  output g2
);

  wire not_1_out, not_2_out, not_3_out, not_4_out, not_5_out, not_6_out, not_7_out;

  not not_1 (not_1_out, erro);
  not not_2 (not_2_out, erro);
  not not_3 (not_3_out, erro);
  not not_4 (not_4_out, erro);
  not not_5 (not_5_out, erro);
  not not_6 (not_6_out, erro);
  not not_7 (not_7_out, erro);
  and and_1 (a2, not_1_out, a);
  and and_2 (b2, not_2_out, b);
  and and_3 (c2, not_3_out, c);
  and and_4 (d2, not_4_out, d);
  and and_5 (e2, not_5_out, e);
  and and_6 (f2, not_6_out, f);
  and and_7 (g2, not_7_out, g);
endmodule
